# Fritzing sketch BMP280 2N7000 LCD 20x4 (saved by Fritzing 0.9.3b)
breadboards: 1

parts:
  Q1 = PNP-Transistor [package="TO92 [THT]"]
  Q2 = PNP-Transistor [package="TO92 [THT]"]
  R1 = Resistor [tolerance=±5% resistance=10k package=THT]
  R2 = Resistor [tolerance=±5% resistance=10k package=THT]
  Bauteil1 = Arduino Uno (Rev3)
  U1 = mystery part, 3 pins [chip_label=BMP280]
  U2 = TMP01 - Low Power, Programmable Temperature Controller [part_number=BMP280]
  LCD1 = LCD screen  # not connected

nets:
  N1: Q1.E, U2.5V
  N2: Q1.B, Q2.B, Bauteil1.3V3, U1.pin1, U2.COMMON, U2.STROBE, U2.VBG, U2.V+
  N3: Q1.C, R2.Pin_0, Bauteil1.A4/SDA
  N4: Q2.E, U1.pin3, U2.10V
  N5: Q2.C, Bauteil1.A5/SCL
  N6: R1.Pin_1, R2.Pin_1, Bauteil1.5V
  N7: Bauteil1.GND, U1.pin2

notes:
  BMP280
  2N7000
  S G D
  VCC GND SCL SDA CSB SDO
