# Fritzing sketch BMP280 MQ135 MQ7 IRLZ34N LCD 20x4 Buzzer LED (saved by Fritzing 0.9.3b)
breadboards: 3

parts:
  U1 = GAS_SENSOR [package=mq-3]
  Q1 = Basic FET N-Channel [package="DPak [SMD]"]
  U2 = GAS_SENSOR [package=mq-3]
  R1 = Resistor [tolerance=±5% resistance=10k package=THT]
  Bauteil1 = Arduino Uno (Rev3)
  LCD1 = LCD screen  # not connected
  R3 = Resistor [tolerance=±5% resistance=100 package=THT]
  R4 = Resistor [tolerance=±5% resistance=100 package=THT]
  U4 = TMP01 - Low Power, Programmable Temperature Controller [part_number=BMP280]
  U5 = mystery part, 3 pins [chip_label=BMP280]
  Q3 = PNP-Transistor [package="TO92 [THT]"]
  Q4 = PNP-Transistor [package="TO92 [THT]"]
  R5 = Resistor [tolerance=±5% resistance=100 package=THT]
  R6 = Resistor [tolerance=±5% resistance=100 package=THT]  # not connected
  J4 = Piezo Speaker
  LED4 = LED - 5mm [color="Yellow (585nm)" package="5 mm [THT]"]
  LED5 = LED - 5mm [color="Green (555nm)" package="5 mm [THT]"]
  LED6 = LED - 5mm [color="Red (633nm)" package="5 mm [THT]"]
  R7 = Resistor [tolerance=±5% resistance=220 package=THT]
  R8 = Resistor [tolerance=±5% resistance=220 package=THT]
  R9 = Resistor [tolerance=±5% resistance=220 package=THT]

nets:
  N1: U1.B1, Q1.source, R1.Pin_1, Bauteil1.GND, U5.pin2, J4.pin1, R7.Pin_0, R8.Pin_0, R9.Pin_0
  N2: U1.A1, U2.B1, Bauteil1.5V
  N3: Q1.Gate, R1.Pin_0, Bauteil1.D13/SCK
  N4: Bauteil1.A4/SDA, R4.Pin_0, Q3.C
  N5: Bauteil1.A5/SCL, Q4.C
  N6: Bauteil1.D8, J4.pin2
  N7: Bauteil1.D10_PWM/SS, LED5.cathode
  N8: Bauteil1.D11_PWM/MOSI, LED4.cathode
  N9: Bauteil1.D12/MISO, LED6.cathode
  N10: R3.Pin_1, R4.Pin_1, U4.COMMON, U4.STROBE, U4.VBG, U4.V+, U5.pin1, Q3.B, Q4.B, R5.Pin_1
  N11: U4.10V, U5.pin3, Q4.E
  N12: U4.5V, Q3.E
  N13: LED4.anode, R8.Pin_1
  N14: LED5.anode, R7.Pin_1
  N15: LED6.anode, R9.Pin_1

notes:
  MQ-7
  MQ-135
  IRLZ34N
  LCD 20X4
  2N7000
  VCC GND SCL SDA CSB SDO
  S G D
  BMP280
