# Fritzing sketch BMP280 MQ135 MQ7 IRLZ34N LCD 20x4 (saved by Fritzing 0.9.3b)
breadboards: 2

parts:
  U1 = GAS_SENSOR [package=mq-3]
  Q1 = Basic FET N-Channel [package="DPak [SMD]"]
  U2 = GAS_SENSOR [package=mq-3]
  R1 = Resistor [tolerance=±5% resistance=10k package=THT]
  Bauteil1 = Arduino Uno (Rev3)
  LCD1 = LCD screen  # not connected
  R3 = Resistor [tolerance=±5% resistance=100 package=THT]
  R4 = Resistor [tolerance=±5% resistance=100 package=THT]
  U4 = TMP01 - Low Power, Programmable Temperature Controller [part_number=BMP280]
  U5 = mystery part, 3 pins [chip_label=BMP280]
  Q3 = PNP-Transistor [package="TO92 [THT]"]
  Q4 = PNP-Transistor [package="TO92 [THT]"]
  R5 = Resistor [tolerance=±5% resistance=100 package=THT]
  R6 = Resistor [tolerance=±5% resistance=100 package=THT]  # not connected

nets:
  N1: U1.B1, Q1.source, R1.Pin_1, Bauteil1.GND, U5.pin2
  N2: U1.A1, U2.B1, Bauteil1.5V
  N3: Q1.Gate, R1.Pin_0, Bauteil1.D13/SCK
  N4: Bauteil1.A4/SDA, R4.Pin_0, Q3.C
  N5: Bauteil1.A5/SCL, Q4.C
  N6: R3.Pin_1, R4.Pin_1, U4.COMMON, U4.STROBE, U4.VBG, U4.V+, U5.pin1, Q3.B, Q4.B, R5.Pin_1
  N7: U4.10V, U5.pin3, Q4.E
  N8: U4.5V, Q3.E

notes:
  MQ-7
  MQ-135
  IRLZ34N
  LCD 20X4
  2N7000
  VCC GND SCL SDA CSB SDO
  S G D
  BMP280
