# Fritzing sketch F18G L293D (saved by Fritzing 0.9.3b)

parts:
  Bauteil1 = Arduino Uno (Rev3)  # not connected
  Composant1 = Rotoshield - Motor driver shield for Arduino
  M2 = DC Motor
  IC1 = L293D [package=THT]  # not connected
  IC2 = L293D [package=THT]
  M1 = DC Motor

nets:
  N1: Composant1.M2-2, M1.pin_2
  N2: Composant1.M2-1, M1.pin_1
  N3: Composant1.M4-1, M2.pin_1
  N4: Composant1.7, IC2.0V
  N5: Composant1.8, IC2.Out_1_(_Controlled_by_Enable_1_)
