# Fritzing sketch HC05Bluetooth Buzzer LED (saved by Fritzing 0.9.3b)
breadboards: 1

parts:
  Bauteil1 = Arduino Uno (Rev3)
  LED2 = LED - 5mm [color="Green (555nm)" package="5 mm [THT]"]
  R3 = Resistor [tolerance=±5% resistance=220 package=THT]
  Bauteil2 = Bluetooth HC-05 Macho  # not connected
  J5 = Piezo Speaker
  R4 = Resistor [tolerance=±5% resistance=1k package=THT]  # not connected
  R5 = Resistor [tolerance=±5% resistance=1k package=THT]  # not connected
  R6 = Resistor [tolerance=±5% resistance=1k package=THT]  # not connected

nets:
  N1: Bauteil1.D8, J5.pin1
  N2: Bauteil1.D10_PWM/SS, LED2.cathode
  N3: Bauteil1.GND, R3.Pin_0, J5.pin2
  N4: LED2.anode, R3.Pin_1
