# Fritzing sketch Joystick LEDs Piezo (saved by Fritzing 0.9.3b)
breadboards: 1

parts:
  Bauteil1 = Arduino Uno (Rev3)
  LED1 = LED - 5mm [color="Red (633nm)" package="5 mm [THT]"]
  LED2 = LED - 5mm [color="Green (555nm)" package="5 mm [THT]"]
  LED3 = LED - 5mm [color="Yellow (585nm)" package="5 mm [THT]"]
  R1 = Resistor [tolerance=±5% resistance=220 package=THT]
  R2 = Resistor [tolerance=±5% resistance=220 package=THT]
  R3 = Resistor [tolerance=±5% resistance=220 package=THT]
  J3 = Piezo Speaker
  Bauteil2 = Arduino Joystick Shield

nets:
  N1: Bauteil1.D8, J3.pin2
  N2: Bauteil1.GND, R1.Pin_0, R2.Pin_0, R3.Pin_0, J3.pin1
  N3: LED1.cathode, Bauteil2.D13
  N4: LED1.anode, R1.Pin_1
  N5: LED2.cathode, Bauteil2.D10
  N6: LED2.anode, R3.Pin_1
  N7: LED3.cathode, Bauteil2.D11
  N8: LED3.anode, R2.Pin_1
