# Fritzing sketch LCDI2CGame (saved by Fritzing 0.9.3b)
breadboards: 1

parts:
  S1 = Pushbutton [package="[THT]"]
  S2 = Pushbutton [package="[THT]"]
  R1 = Resistor [tolerance=±5% resistance=220 package=THT]
  R2 = Resistor [tolerance=±5% resistance=220 package=THT]
  Part1 = Arduino Uno (Rev3)
  LCD1 = LCD screen  # not connected

nets:
  N1: S1.Pin_1, S1.Pin_2, S2.Pin_1, S2.Pin_2, Part1.5V
  N2: S1.Pin_3, S1.Pin_4, R2.Pin_1
  N3: S2.Pin_3, S2.Pin_4, R1.Pin_1, Part1.D2
  N4: R1.Pin_0, R2.Pin_0, Part1.GND
