# Fritzing sketch LDR LED (saved by Fritzing 0.9.3b)
breadboards: 1

parts:
  Bauteil1 = Arduino Uno (Rev3)
  R1 = Photocell (LDR) [package=THT]
  R2 = Resistor [tolerance=±5% resistance=220 package=THT]
  LED1 = smd LED [color="Red (633nm)" package="0805 [SMD]"]
  R3 = Resistor [tolerance=±5% resistance=220 package=THT]

nets:
  N1: Bauteil1.A0, R1.pin_0, R2.Pin_1
  N2: Bauteil1.D9_PWM, LED1.cathode
  N3: Bauteil1.5V, R1.pin_1
  N4: Bauteil1.GND, R2.Pin_0, R3.Pin_0
  N5: LED1.anode, R3.Pin_1
