# Fritzing sketch MAX4466 LEDs Piezo (saved by Fritzing 0.9.3b)
breadboards: 1

parts:
  Bauteil1 = Arduino Uno (Rev3)
  LED2 = LED - 5mm [color="Green (555nm)" package="5 mm [THT]"]
  R3 = Resistor [tolerance=±5% resistance=220 package=THT]
  J3 = Piezo Speaker
  SPKR1 = Loudspeaker

nets:
  N1: Bauteil1.D8, J3.pin2
  N2: Bauteil1.D9_PWM, LED2.cathode
  N3: Bauteil1.3V3, SPKR1.pin2
  N4: Bauteil1.GND, J3.pin1, SPKR1.pin1
  N5: LED2.anode, R3.Pin_1

notes:
  MAX4466 Electret
