# Fritzing sketch MQ135 MQ7 IRLZ34N LCD 20x4 (saved by Fritzing 0.9.3b)
breadboards: 1

parts:
  U1 = GAS_SENSOR [package=mq-3]
  Q1 = Basic FET N-Channel [package="DPak [SMD]"]
  U2 = GAS_SENSOR [package=mq-3]
  R1 = Resistor [tolerance=±5% resistance=10k package=THT]
  Bauteil1 = Arduino Uno (Rev3)
  LCD1 = LCD screen  # not connected

nets:
  N1: U1.B1, Q1.source, R1.Pin_1, Bauteil1.GND
  N2: U1.A1, U2.B1, Bauteil1.5V
  N3: Q1.Gate, R1.Pin_0, Bauteil1.D13/SCK

notes:
  MQ-7
  MQ-135
  IRLZ34N
  LCD 20X4
