# Fritzing sketch MQ7 IRLZ34N (saved by Fritzing 0.9.3b)
breadboards: 1

parts:
  Q1 = Basic FET N-Channel [package="DPak [SMD]"]
  U2 = GAS_SENSOR [package=mq-3]
  R1 = Resistor [tolerance=±5% resistance=10k package=THT]
  Bauteil1 = Arduino Uno (Rev3)
  LCD2 = LCD screen  # not connected
  LED3 = LED - 5mm [color="Green (555nm)" package="5 mm [THT]"]
  LED4 = LED - 5mm [color="Yellow (585nm)" package="5 mm [THT]"]
  LED5 = LED - 5mm [color="Red (660nm)" package="5 mm [THT]"]  # not connected
  R2 = Resistor [tolerance=±5% resistance=220 package=THT]
  R3 = Resistor [tolerance=±5% resistance=220 package=THT]
  R4 = Resistor [tolerance=±5% resistance=220 package=THT]

nets:
  N1: Q1.Gate, R1.Pin_0, Bauteil1.D13/SCK
  N2: Q1.source, R1.Pin_1, Bauteil1.GND, R2.Pin_0, R4.Pin_0
  N3: U2.B1, Bauteil1.5V
  N4: Bauteil1.D8, LED3.anode
  N5: Bauteil1.D9_PWM, LED4.anode
  N6: LED3.cathode, R4.Pin_1
  N7: LED4.cathode, R3.Pin_1

notes:
  MQ-7
  IRLZ34N
  LCD 20X4 with I2C
