# Fritzing sketch MicroServo LEDs (saved by Fritzing 0.9.3b)
breadboards: 1

parts:
  Bauteil1 = Arduino Uno (Rev3)
  LED1 = LED - 5mm [color="Red (633nm)" package="5 mm [THT]"]
  LED2 = LED - 5mm [color="Green (555nm)" package="5 mm [THT]"]
  LED3 = LED - 5mm [color="Yellow (585nm)" package="5 mm [THT]"]
  R1 = Resistor [tolerance=±5% resistance=220 package=THT]
  R2 = Resistor [tolerance=±5% resistance=220 package=THT]
  R3 = Resistor [tolerance=±5% resistance=220 package=THT]
  J2 = Basic Servo

nets:
  N1: Bauteil1.D9_PWM, LED2.cathode
  N2: Bauteil1.D10_PWM/SS, LED3.cathode
  N3: Bauteil1.D12/MISO, LED1.cathode
  N4: Bauteil1.D6_PWM, J2.pulse
  5V: Bauteil1.5V, J2.vcc
  GND: Bauteil1.GND, J2.gnd
  N5: LED1.anode, R1.Pin_1
  N6: LED2.anode, R3.Pin_1
  N7: LED3.anode, R2.Pin_1
  N8: R1.Pin_0, R2.Pin_0, R3.Pin_0
