# Fritzing sketch MicroServo SG90 (saved by Fritzing 0.9.3b)

parts:
  Bauteil1 = Arduino Uno (Rev3)
  J1 = Basic Servo

nets:
  N1: Bauteil1.D6_PWM, J1.pulse
  5V: Bauteil1.5V, J1.vcc
  GND: Bauteil1.GND, J1.gnd
