# Fritzing sketch NRF24L01 (saved by Fritzing 0.9.3b)
breadboards: 1

parts:
  Bauteil1 = Arduino Uno (Rev3)
  LED2 = LED - 5mm [color="Green (555nm)" package="5 mm [THT]"]
  R3 = Resistor [tolerance=±5% resistance=220 package=THT]
  Bauteil2 = NRF24L01

nets:
  N1: Bauteil1.D9_PWM, Bauteil2.CE
  N2: Bauteil1.D10_PWM/SS, Bauteil2.MOSI
  N3: Bauteil1.D11_PWM/MOSI, Bauteil2.CSN
  N4: Bauteil1.D12/MISO, Bauteil2.MISO
  N5: Bauteil1.D13/SCK, Bauteil2.SCK
  N6: Bauteil1.D7, LED2.cathode
  3V3: Bauteil1.3V3, Bauteil2.VCC
  GND: Bauteil1.GND, Bauteil2.GND
  N7: LED2.anode, R3.Pin_1
