# Fritzing sketch PCB1 (saved by Fritzing 0.9.3b)
breadboards: 1

parts:
  Bauteil1 = Arduino Uno (Rev3) - ICSP
  LED1 = LED - 5mm [color="Red (633nm)" package="5 mm [THT]"]
  LED2 = LED - 5mm [color="Red (633nm)" package="5 mm [THT]"]
  J1 = Piezo Speaker
  R1 = Resistor [tolerance=±5% resistance=220 package=THT]
  R2 = Resistor [tolerance=±5% resistance=220 package=THT]

nets:
  N1: Bauteil1.D8, J1.pin2
  N2: Bauteil1.D10_PWM/SS, LED1.cathode
  N3: Bauteil1.D5_PWM, LED2.cathode
  N4: Bauteil1.GND, J1.pin1, R1.Pin_0
  N5: LED1.anode, R1.Pin_1
  N6: LED2.anode, R2.Pin_1
