# Fritzing sketch PIR LED (saved by Fritzing 0.9.3b)
breadboards: 1

parts:
  Bauteil1 = Arduino Uno (Rev3)
  LED2 = LED - 5mm [color="Green (555nm)" package="5 mm [THT]"]
  R3 = Resistor [tolerance=±5% resistance=220 package=THT]
  U1 = MLX90614 [package=to-39]  # not connected

nets:
  N1: Bauteil1.D9_PWM, LED2.cathode
  N2: Bauteil1.GND, R3.Pin_0
  N3: LED2.anode, R3.Pin_1
