# Fritzing sketch Piezo Buzzer Detect Knocking (saved by Fritzing 0.9.3b)
breadboards: 1

parts:
  Bauteil1 = Arduino Uno (Rev3)
  J1 = Piezo Speaker
  LED1 = LED - 5mm [color="Red (633nm)" package="5 mm [THT]"]
  R1 = Resistor [tolerance=±5% resistance=220 package=THT]

nets:
  N1: Bauteil1.A5/SCL, J1.pin2
  N2: Bauteil1.D13/SCK, LED1.cathode
  N3: Bauteil1.GND, J1.pin1, R1.Pin_1
  N4: LED1.anode, R1.Pin_0
