# Fritzing sketch Project Piano by Distance  (saved by Fritzing 0.9.3b)
breadboards: 1

parts:
  Bauteil1 = Arduino Uno (Rev3)
  J1 = Piezo Speaker
  LED1 = LED - 5mm [color="Red (633nm)" package="5 mm [THT]"]
  LED2 = LED - 5mm [color="Green (555nm)" package="5 mm [THT]"]
  LED3 = LED - 5mm [color="Yellow (585nm)" package="5 mm [THT]"]
  R1 = Resistor [tolerance=±5% resistance=220 package=THT]
  R2 = Resistor [tolerance=±5% resistance=220 package=THT]
  R3 = Resistor [tolerance=±5% resistance=220 package=THT]
  hc-sr1 = hc-sr04

nets:
  N1: Bauteil1.D9_PWM, LED2.cathode
  N2: Bauteil1.D10_PWM/SS, LED3.cathode
  N3: Bauteil1.D11_PWM/MOSI, J1.pin2
  N4: Bauteil1.D12/MISO, LED1.cathode
  N5: Bauteil1.GND, J1.pin1
  N6: Bauteil1.D2, hc-sr1.VCC
  N7: Bauteil1.D3_PWM, hc-sr1.Trig
  N8: Bauteil1.D4, hc-sr1.Echo
  N9: Bauteil1.D5_PWM, hc-sr1.GND
  N10: LED1.anode, R1.Pin_1
  N11: LED2.anode, R3.Pin_1
  N12: LED3.anode, R2.Pin_1
  N13: R1.Pin_0, R2.Pin_0, R3.Pin_0
