# Fritzing sketch RF433 Transmitter MQ135 MQ7 IRLZ34N (saved by Fritzing 0.9.3b)
breadboards: 1

parts:
  U1 = GAS_SENSOR [package=mq-3]
  Q1 = Basic FET N-Channel [package="DPak [SMD]"]
  U2 = GAS_SENSOR [package=mq-3]
  R1 = Resistor [tolerance=±5% resistance=10k package=THT]
  RFM12b1 = RFM12b HopeRF Transceiver
  Bauteil1 = Arduino Uno (Rev3)
  LCD2 = LCD screen  # not connected

nets:
  N1: U1.B1, Q1.source, R1.Pin_1, RFM12b1.11_nINT/VDI, Bauteil1.GND
  N2: U1.A1, U2.B1, RFM12b1.10_GND, Bauteil1.5V
  N3: Q1.Gate, R1.Pin_0, Bauteil1.D13/SCK

notes:
  MQ-7
  MQ-135
  IRLZ34N
  RF433 Transmitter
