# Fritzing sketch Vibration Motor BMP280 2N7000 ST7789 GPS Neo6M (saved by Fritzing 0.9.3b)
breadboards: 1

parts:
  Q1 = PNP-Transistor [package="TO92 [THT]"]
  Q2 = PNP-Transistor [package="TO92 [THT]"]
  R1 = Resistor [tolerance=±5% resistance=10k package=THT]
  R2 = Resistor [tolerance=±5% resistance=10k package=THT]
  Bauteil1 = Arduino Uno (Rev3)
  U1 = mystery part, 3 pins [chip_label=BMP280]
  U2 = TMP01 - Low Power, Programmable Temperature Controller [part_number=BMP280]
  R3 = Resistor [tolerance=±5% resistance=1 package=THT]
  R4 = Resistor [tolerance=±5% resistance=2.2 package=THT]
  U5 = mystery part, 3 pins [chip_label="Vibration Motor"]

nets:
  N1: Q1.E, U2.5V
  N2: Q1.B, Q2.B, R1.Pin_1, R2.Pin_1, Bauteil1.GND, U1.pin1, U1.pin2, U2.COMMON, U2.STROBE, U2.VBG, U2.V+, R3.Pin_0, R4.Pin_0, R4.Pin_1, U5.pin1
  N3: Q1.C, R2.Pin_0, Bauteil1.A4/SDA
  N4: Q2.E, U1.pin3, U2.10V
  N5: Q2.C, Bauteil1.A5/SCL
  N6: Bauteil1.D3_PWM, U5.pin3
  N7: Bauteil1.5V, R3.Pin_1, U5.pin2

notes:
  BMP280
  2N7000
  S G D
  VCC GND SCL SDA CSB SDO
  SCL SDA RES DC
  ST7789
  GND Connector
  GND for ST7789
  2K Ohm Resistor
  1K Ohm Resistor
  3v3 VCC for ST7789
  GND VCC IN
  Vibration Motor
