# Fritzing sketch nRF24L01 BMP280 Rx (saved by Fritzing 0.9.3b)

parts:
  Bauteil1 = Arduino Uno (Rev3)
  Composant1 = NRF24L01+ Breakout Board
  LCD2 = LCD screen  # not connected

nets:
  N1: Bauteil1.D9_PWM, Composant1.CE
  N2: Bauteil1.D10_PWM/SS, Composant1.CS
  N3: Bauteil1.D11_PWM/MOSI, Composant1.MOSI
  N4: Bauteil1.D12/MISO, Composant1.MISO
  N5: Bauteil1.D13/SCK, Composant1.SCK
  3V3: Bauteil1.3V3, Composant1.VCC
  GND: Bauteil1.GND, Composant1.GND
