# Fritzing sketch nRF24L01 BMP280 Tx (saved by Fritzing 0.9.3b)
breadboards: 1

parts:
  Bauteil1 = Arduino Uno (Rev3)
  R3 = Resistor [tolerance=±5% resistance=100 package=THT]
  R4 = Resistor [tolerance=±5% resistance=100 package=THT]
  U4 = TMP01 - Low Power, Programmable Temperature Controller [part_number=BMP280]
  U5 = mystery part, 3 pins [chip_label=BMP280]
  Q3 = PNP-Transistor [package="TO92 [THT]"]
  Q4 = PNP-Transistor [package="TO92 [THT]"]
  R5 = Resistor [tolerance=±5% resistance=100 package=THT]
  R6 = Resistor [tolerance=±5% resistance=100 package=THT]  # not connected
  Composant1 = NRF24L01+ Breakout Board

nets:
  N1: Bauteil1.A4/SDA, R4.Pin_0, Q3.C
  N2: Bauteil1.A5/SCL, Q4.C
  N3: Bauteil1.D9_PWM, Composant1.CE
  N4: Bauteil1.D10_PWM/SS, Composant1.CS
  N5: Bauteil1.D11_PWM/MOSI, Composant1.MOSI
  N6: Bauteil1.D12/MISO, Composant1.MISO
  N7: Bauteil1.D13/SCK, Composant1.SCK
  5V: Bauteil1.5V, Composant1.VCC
  GND: Bauteil1.GND, R3.Pin_1, R4.Pin_1, U4.COMMON, U4.STROBE, U4.VBG, U4.V+, U5.pin1, U5.pin2, Q3.B, Q4.B, R5.Pin_1, Composant1.GND
  N8: U4.10V, U5.pin3, Q4.E
  N9: U4.5V, Q3.E

notes:
  2N7000
  VCC GND SCL SDA CSB SDO
  S G D
  BMP280
